# Fritzing sketch dice (saved by Fritzing 0.9.4)
breadboards: 1

parts:
  Part1 = Arduino Uno (Rev3)
  LED1 = LED - 5mm [color="Green (560nm)" package="5 mm [THT]"]
  LED2 = LED - 5mm [color="Green (560nm)" package="5 mm [THT]"]
  LED3 = LED - 5mm [color="Green (560nm)" package="5 mm [THT]"]
  LED4 = LED - 5mm [color="Green (560nm)" package="5 mm [THT]"]
  LED5 = LED - 5mm [color="Green (560nm)" package="5 mm [THT]"]
  LED6 = LED - 5mm [color="Green (560nm)" package="5 mm [THT]"]
  R1 = Resistor [tolerance=±5% resistance=180 package=THT]
  R2 = Resistor [tolerance=±5% resistance=180 package=THT]
  R3 = Resistor [tolerance=±5% resistance=180 package=THT]
  R4 = Resistor [tolerance=±5% resistance=180 package=THT]
  R5 = Resistor [tolerance=±5% resistance=180 package=THT]
  R6 = Resistor [tolerance=±5% resistance=180 package=THT]
  S1 = Pushbutton [package="[THT]"]

nets:
  N1: Part1.D2, LED1.anode
  N2: Part1.D3_PWM, LED6.anode
  N3: Part1.D4, LED5.anode
  N4: Part1.D5_PWM, LED4.anode
  N5: Part1.D6_PWM, LED3.anode
  N6: Part1.D7, LED2.anode
  N7: Part1.RESET, S1.Pin_1, S1.Pin_2
  N8: Part1.GND, R1.Pin_1, R2.Pin_1, R3.Pin_1, R4.Pin_1, R5.Pin_1, R6.Pin_1, S1.Pin_3, S1.Pin_4
  N9: LED1.cathode, R1.Pin_0
  N10: LED2.cathode, R2.Pin_0
  N11: LED3.cathode, R3.Pin_0
  N12: LED4.cathode, R4.Pin_0
  N13: LED5.cathode, R5.Pin_0
  N14: LED6.cathode, R6.Pin_0
